# Fritzing sketch MP3Player (saved by Fritzing 1.0.2b)
breadboards: 1

parts:
  A1 = Particle - Photon2
  DFRobot_DFPlayer_Mini1 = DFRobot DFPlayer Mini [part_number=DFR0299]
  SP1 = SPEAKER [package=pcb_mount_speaker]

nets:
  N1: A1.Pin_2, A1.Pin_31, DFRobot_DFPlayer_Mini1.VCC
  N2: A1.Pin_4, A1.Pin_30, DFRobot_DFPlayer_Mini1.GND-1, DFRobot_DFPlayer_Mini1.GND-2
  N3: A1.Pin_14, DFRobot_DFPlayer_Mini1.TX
  N4: A1.Pin_15, DFRobot_DFPlayer_Mini1.RX
  N5: DFRobot_DFPlayer_Mini1.SPK_1, SP1.-
  N6: DFRobot_DFPlayer_Mini1.SPK_2, SP1.+

custom parts:
  Particle - Photon2: The Photon 2 is a microcontroller and Wi-Fi networking developed by particle. Features: 802.11a/b/g/n Wi-Fi, 2.4 GHz and 5 GHz Integrated PCB antenna Integrated U.FL connector for external antenna Integrated RF switch BLE 5 using same antenna as Wi-Fi Realtek RTL8721DM MCU ARM Cortex M33 CPU, 200 MHz 2048 KB (2 MB) user application maximum size 3072 KB (3 MB) of RAM available to user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
